# Fritzing sketch IR_Array (saved by Fritzing 0.9.5d)

parts:
  U2 = TCRT5000 [package=THT]
  U3 = TCRT5000 [package=THT]
  U4 = TCRT5000 [package=THT]
  U5 = TCRT5000 [package=THT]
  U6 = TCRT5000 [package=THT]
  U7 = TCRT5000 [package=THT]
  U8 = TCRT5000 [package=THT]
  ADC1 = MCP3008 [package=dil16]
  R13 = Resistor [tolerance=±5% resistance=10k package=THT]
  R14 = Resistor [tolerance=±5% resistance=510 package=THT]
  R15 = Resistor [tolerance=±5% resistance=10k package=THT]
  R16 = Resistor [tolerance=±5% resistance=510 package=THT]
  R17 = Resistor [tolerance=±5% resistance=10k package=THT]
  R18 = Resistor [tolerance=±5% resistance=510 package=THT]
  R2 = Resistor [tolerance=±5% resistance=10k package=THT]
  U1 = TCRT5000 [package=THT]
  R19 = Resistor [tolerance=±5% resistance=10k package=THT]
  R20 = Resistor [tolerance=±5% resistance=510 package=THT]
  R21 = Resistor [tolerance=±5% resistance=10k package=THT]
  R22 = Resistor [tolerance=±5% resistance=510 package=THT]
  R23 = Resistor [tolerance=±5% resistance=10k package=THT]
  R24 = Resistor [tolerance=±5% resistance=510 package=THT]
  R25 = Resistor [tolerance=±5% resistance=10k package=THT]
  R27 = Resistor [tolerance=±5% resistance=510 package=THT]
  R26 = Resistor [tolerance=±5% resistance=510 package=THT]
  Power_plug1 = Power plug

nets:
  N1: U2.Pin_1, ADC1.CH6, R13.Pin_1
  N2: U2.Pin_2, U2.Pin_3, U3.Pin_2, U3.Pin_3, U4.Pin_2, U4.Pin_3, U5.Pin_2, U5.Pin_3, U6.Pin_2, U6.Pin_3, U7.Pin_2, U7.Pin_3, U8.Pin_2, U8.Pin_3, U1.Pin_2, U1.Pin_3, Power_plug1.GND
  N3: U2.Pin_4, R14.Pin_1
  N4: U3.Pin_1, ADC1.CH5, R15.Pin_1
  N5: U3.Pin_4, R16.Pin_1
  N6: U4.Pin_1, ADC1.CH4, R17.Pin_1
  N7: U4.Pin_4, R18.Pin_1
  N8: U5.Pin_1, ADC1.CH3, R19.Pin_1
  N9: U5.Pin_4, R20.Pin_1
  N10: U6.Pin_1, ADC1.CH2, R21.Pin_1
  N11: U6.Pin_4, R22.Pin_1
  N12: U7.Pin_1, ADC1.CH1, R23.Pin_1
  N13: U7.Pin_4, R24.Pin_1
  N14: U8.Pin_1, ADC1.CH0, R25.Pin_1
  N15: U8.Pin_4, R26.Pin_1
  N16: ADC1.CH7, R2.Pin_1, U1.Pin_1
  N17: U1.Pin_4, R27.Pin_1
  N18: R27.Pin_0, Power_plug1.VCC

custom parts:
  TCRT5000: TCRT5000 optical reflective sensor
