# Fritzing sketch Plex (saved by Fritzing 0.9.5d)

parts:
  Raspberry_Pi1 = Raspberry Pi B+
  M1 = Getriebemotor
  M2 = Getriebemotor
  L298N1 = L298N DC motor driver
  M3 = RioRand LM2596
  BAT1 = Battery Holders [package=battery-aa]  # not connected
  BAT2 = Battery Holders [package=battery-aa]
  BAT3 = Battery Holders [package=battery-aa]
  BAT4 = Battery Holders [package=battery-aa]
  BAT5 = Battery Holders [package=battery-aa]
  BAT6 = Battery Holders [package=battery-aa]
  IC1 = Rasberry Pi NIOR Camera [chip_label=IC package="DIP (Dual Inline) [THT]"]  # not connected
  M4 = RioRand LM2596
  Part2 = ADS1115
  J10 = Infrared Proximity Sensor
  J11 = Infrared Proximity Sensor
  J12 = Infrared Proximity Sensor
  JP3 = USB_MICROB_PLUG [package=micro-b-ra-th]
  U9 = TCRT5000 [package=THT]
  U10 = TCRT5000 [package=THT]
  U11 = TCRT5000 [package=THT]
  U12 = TCRT5000 [package=THT]
  U13 = TCRT5000 [package=THT]
  U14 = TCRT5000 [package=THT]
  U15 = TCRT5000 [package=THT]
  U16 = TCRT5000 [package=THT]
  ADC2 = MCP3008 [package=dil16]
  R28 = Resistor [tolerance=±5% resistance=510 package=THT]
  R29 = Resistor [tolerance=±5% resistance=510 package=THT]
  R30 = Resistor [tolerance=±5% resistance=10k package=THT]
  R31 = Resistor [tolerance=±5% resistance=510 package=THT]
  R32 = Resistor [tolerance=±5% resistance=10k package=THT]
  R33 = Resistor [tolerance=±5% resistance=510 package=THT]
  R34 = Resistor [tolerance=±5% resistance=10k package=THT]
  R35 = Resistor [tolerance=±5% resistance=510 package=THT]
  R36 = Resistor [tolerance=±5% resistance=10k package=THT]
  R37 = Resistor [tolerance=±5% resistance=10k package=THT]
  R38 = Resistor [tolerance=±5% resistance=510 package=THT]
  R39 = Resistor [tolerance=±5% resistance=10k package=THT]
  R40 = Resistor [tolerance=±5% resistance=510 package=THT]
  R41 = Resistor [tolerance=±5% resistance=10k package=THT]
  R42 = Resistor [tolerance=±5% resistance=510 package=THT]
  R43 = Resistor [tolerance=±5% resistance=10k package=THT]
  L298N2 = L298N DC motor driver
  M5 = DC Motor  # not connected
  M6 = DC Motor  # not connected
  M7 = Stepper Motor - Bipolar
  DRV_1 = DRV 8825 Stepper Motor Carrier, High Current [part_number="DRV 8825"]

nets:
  3V3: Raspberry_Pi1.3V3, J12.Vcc
  N1: Raspberry_Pi1.GPIO5, DRV_1.DIRECTION
  N2: Raspberry_Pi1.GPIO6, DRV_1.STEP
  N3: Raspberry_Pi1.GPIO13, L298N1.ENB
  N4: Raspberry_Pi1.GPIO19, DRV_1.SLEEP
  N5: Raspberry_Pi1.GPIO26, L298N2.IN4
  GND: Raspberry_Pi1.GND, L298N1.GND, J12.GND, ADC2.CS/SHDN, ADC2.CLK, R37.Pin_0, L298N2.GND, DRV_1.GROUND_ST/_MT
  N6: Raspberry_Pi1.GPIO21, L298N2.IN3
  N7: Raspberry_Pi1.GPIO20, L298N2.IN2
  N8: Raspberry_Pi1.GPIO12, L298N1.ENA
  N9: Raspberry_Pi1.ID_SC, L298N1.IN4
  N10: Raspberry_Pi1.GPIO7, L298N1.IN3
  N11: Raspberry_Pi1.GPIO8, L298N1.IN2
  N12: Raspberry_Pi1.GPIO25, L298N1.IN1
  N13: Raspberry_Pi1.GPIO24, ADC2.Dout
  N14: Raspberry_Pi1.GPIO23, ADC2.Din
  N15: Raspberry_Pi1.GPIO18, Part2.SCL
  N16: Raspberry_Pi1.GPIO15, Part2.SDA
  N17: Raspberry_Pi1.GPIO14, Part2.ADDR
  N18: M1.pin_1, L298N1.OUT2
  N19: M1.pin_2, L298N1.OUT1
  N20: M2.pin_1, L298N1.OUT4
  N21: M2.pin_2, L298N1.OUT3
  N22: L298N1.12V, M3.Pin_3
  N23: BAT2.-, BAT5.+
  N24: BAT2.+, BAT4.-
  N25: BAT3.-, BAT6.+
  N26: BAT3.+, BAT5.-
  N27: BAT6.-, M4.Pin_2
  N28: M4.Pin_3, JP3.VCC
  N29: M4.Pin_4, JP3.D+
  VCC: Part2.VDD, J10.Vcc, J11.Vcc
  GND_2: Part2.GND, J10.GND, J11.GND
  N30: Part2.A0, J12.Vout
  N31: Part2.A1, J11.Vout
  N32: Part2.A2, J10.Vout
  N33: U9.Pin_1, ADC2.CH7, R37.Pin_1
  N34: U9.Pin_3, U10.Pin_2, U10.Pin_3, U11.Pin_2, U11.Pin_3, U12.Pin_2, U12.Pin_3, U13.Pin_2, U13.Pin_3, U14.Pin_2, U14.Pin_3, U15.Pin_2, U15.Pin_3, U16.Pin_2, U16.Pin_3
  N35: U9.Pin_4, R29.Pin_1
  N36: U10.Pin_1, ADC2.CH0, R30.Pin_1
  N37: U10.Pin_4, R28.Pin_1
  N38: U11.Pin_1, ADC2.CH1, R32.Pin_1
  N39: U11.Pin_4, R31.Pin_1
  N40: U12.Pin_1, ADC2.CH2, R34.Pin_1
  N41: U12.Pin_4, R33.Pin_1
  N42: U13.Pin_1, ADC2.CH3, R36.Pin_1
  N43: U13.Pin_4, R35.Pin_1
  N44: U14.Pin_1, ADC2.CH4, R39.Pin_1
  N45: U14.Pin_4, R38.Pin_1
  N46: U15.Pin_1, ADC2.CH5, R41.Pin_1
  N47: U15.Pin_4, R40.Pin_1
  N48: U16.Pin_1, ADC2.CH6, R43.Pin_1
  N49: U16.Pin_4, R42.Pin_1
  N50: ADC2.VREF, ADC2.VDD
  N51: M7.A, DRV_1.OUT_2B
  N52: M7.C, DRV_1.OUT_2A
  N53: M7.B, DRV_1.OUT_1A
  N54: M7.D, DRV_1.OUT_1B

custom parts:
  L298N DC motor driver: 2x DC motor driver with 78M05 positive voltage regulator (7..35 V) L298N: max 46 V, 2 A Set 5 V Enable jumper to enable 5 V regultor (needed for the L298N) and +5 V output at screw terminal or supply external +5 V at screw terminal Set ENA and/or ENB to +5 V to enable motor permanently or supply ENA and/or ENB with PWM signal IN1 and IN2 set rotation directory for motor A (OUT1/OUT2) IN2 and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
  Rasberry Pi NIOR Camera: Camera
  ADS1115: ADC ADS1115
  TCRT5000: TCRT5000 optical reflective sensor
