# Fritzing sketch ir3+ADC (saved by Fritzing 0.9.5d)

parts:
  Part1 = ADS1115
  J7 = Infrared Proximity Sensor
  J8 = Infrared Proximity Sensor
  J9 = Infrared Proximity Sensor

nets:
  VCC: Part1.VDD, J7.Vcc, J8.Vcc, J9.Vcc
  GND: Part1.GND, J7.GND, J8.GND, J9.GND
  N1: Part1.A0, J9.Vout
  N2: Part1.A1, J8.Vout
  N3: Part1.A2, J7.Vout

custom parts:
  ADS1115: ADC ADS1115
